// Logisim project Milestone 1.circ as structural Verilog: 3 circuits, main circuit main
module main (
  input  En_R,
  input  En_W,
  input  in_3,
  input  in_4,
  input  in_5,
  input  Clear,
  input  [2:0] in_7,
  input  Clear_2,
  input  in_9,
  input  in_10,
  input  Clear_3,
  input  [2:0] in_12,
  output [15:0] out_13,
  output E
);

  wire clock_1_out;
  wire [6:0] AR_q, bit_extender_2_out;
  wire [15:0] AC_q, alumux_1_out, bit_extender_1_out, DR_q, ram_1_data, TR_q;

  Clock clock_1 (.out(clock_1_out));
  Register #(.width(7)) AR (.D(bit_extender_2_out), .en(in_3), .Q(AR_q), .clk(clock_1_out), .clr(in_4));
  Register #(.width(16)) TR (.D(out_13), .en(in_5), .Q(TR_q), .clk(clock_1_out), .clr(Clear));
  Register #(.width(16)) AC (.D(alumux_1_out), .en(in_10), .Q(AC_q), .clk(clock_1_out), .clr(Clear_3));
  Register #(.width(16)) DR (.D(out_13), .en(in_9), .Q(DR_q), .clk(clock_1_out), .clr(Clear_2));
  RAM #(.addrWidth(7), .dataWidth(16), .bus("separate")) ram_1 (
    .addr(AR_q), .din(out_13), .data(ram_1_data), .str(En_W), .clk(clock_1_out), .ld(En_R));  // open: sel, clr
  assign bit_extender_1_out = {{9{1'b0}}, AR_q};  // Bit_Extender bit_extender_1
  Multiplexer #(.select(3), .width(16), .enable("false")) multiplexer_1 (
    .in0(ram_1_data), .in1(bit_extender_1_out), .in2(TR_q), .in3(DR_q), .in4(AC_q), .out(out_13), .sel(in_7));  // open: in5, in6, in7
  ALUMUX alumux_1 (.A(DR_q), .B(AC_q), .C2C1C0(in_12), .OUT(alumux_1_out), .E(E));
  Bit_Extender #(.in_width(16), .out_width(7)) bit_extender_2 (.in(out_13), .out(bit_extender_2_out));

  // Notes on the sheet:
  //   memory 128 X 16
endmodule

module ALU (
  input  [15:0] A,
  input  [15:0] B,
  input  [2:0] C2C1C0,
  output [15:0] OUT,
  output E
);

  wire adder_1_cout, adder_2_cout, and_2_out, and_3_out, and_4_out, not_1_out, not_2_out, not_3_out,
       not_4_out, subtractor_1_bout;
  wire [15:0] adder_1_out, adder_2_out, and_1_out, or_1_out, subtractor_1_out, xor_1_out;

  Adder #(.width(16)) adder_1 (.a(A), .b(B), .out(adder_1_out), .cin(1'b0), .cout(adder_1_cout));
  Subtractor #(.width(16)) subtractor_1 (.a(A), .b(B), .out(subtractor_1_out), .bin(1'b0), .bout(subtractor_1_bout));
  assign and_1_out = A & B;  // AND_Gate and_1, 16 bits wide
  assign or_1_out = A | B;  // OR_Gate or_1, 16 bits wide
  assign xor_1_out = A ^ B;  // XOR_Gate xor_1, 16 bits wide
  Adder #(.width(16)) adder_2 (.a(A), .b(16'h1), .out(adder_2_out), .cin(1'b0), .cout(adder_2_cout));
  Multiplexer #(.select(3), .width(16), .enable("false")) multiplexer_1 (
    .in1(adder_1_out), .in2(subtractor_1_out), .in3(A), .in4(and_1_out), .in5(or_1_out), .in6(xor_1_out),
    .in7(adder_2_out), .out(OUT), .sel(C2C1C0));  // open: in0
  not not_1 (not_1_out, C2C1C0[1]);
  not not_2 (not_2_out, C2C1C0[2]);
  not not_3 (not_3_out, C2C1C0[0]);
  not not_4 (not_4_out, C2C1C0[2]);
  and and_2 (and_2_out, C2C1C0[0], not_1_out, not_2_out, adder_1_cout);
  and and_3 (and_3_out, not_3_out, C2C1C0[1], not_4_out, subtractor_1_bout);
  and and_4 (and_4_out, C2C1C0[0], C2C1C0[1], C2C1C0[2], adder_2_cout);
  or or_2 (E, and_2_out, and_3_out, and_4_out);
endmodule

module ALUMUX (
  input  [15:0] A,
  input  [15:0] B,
  input  [2:0] C2C1C0,
  output [15:0] OUT,
  output E
);

  wire adder_1_cout, adder_2_cout, subtractor_1_bout;
  wire [15:0] adder_1_out, adder_2_out, and_1_out, or_1_out, subtractor_1_out, xor_1_out;

  Adder #(.width(16)) adder_1 (.a(A), .b(B), .out(adder_1_out), .cin(1'b0), .cout(adder_1_cout));
  Subtractor #(.width(16)) subtractor_1 (.a(A), .b(B), .out(subtractor_1_out), .bin(1'b0), .bout(subtractor_1_bout));
  assign and_1_out = A & B;  // AND_Gate and_1, 16 bits wide
  assign or_1_out = A | B;  // OR_Gate or_1, 16 bits wide
  assign xor_1_out = A ^ B;  // XOR_Gate xor_1, 16 bits wide
  Adder #(.width(16)) adder_2 (.a(A), .b(16'h1), .out(adder_2_out), .cin(1'b0), .cout(adder_2_cout));
  Multiplexer #(.select(3), .width(16), .enable("false")) multiplexer_1 (
    .in1(adder_1_out), .in2(subtractor_1_out), .in3(A), .in4(and_1_out), .in5(or_1_out), .in6(xor_1_out),
    .in7(adder_2_out), .out(OUT), .sel(C2C1C0));  // open: in0
  Multiplexer #(.select(3), .enable("false")) multiplexer_2 (
    .in0(1'b0), .in1(adder_1_cout), .in2(subtractor_1_bout), .in3(1'b0), .in4(1'b0), .in5(1'b0), .in6(1'b0),
    .in7(adder_2_cout), .out(E), .sel(C2C1C0));
endmodule
