// Logisim project Milestone 2.circ as structural Verilog: 4 circuits, main circuit main
module main (
  input  in_1,
  input  Clear,
  input  Clear_2,
  input  Clear_3,
  output [15:0] out_5,
  output E
);

  wire AC_out, and_1_out, and_2_out, and_3_out, and_4_out, and_5_out, and_6_out, and_7_out, and_8_out,
       and_9_out, and_10_out, and_11_out, and_12_out, and_13_out, and_14_out, and_16_out, and_17_out,
       and_18_out, and_19_out, and_20_out, and_21_out, and_23_out, and_24_out, and_25_out, and_26_out,
       and_27_out, AR_out, B0, B1, B2, B3, B4, B5, B6, B7, B8, B9, B10, B11, CLK, clr_SC, D0, D1, D2, D3, D4,
       D5, D6, D7, d_ff_1_q, en_AC, en_AR, en_DR, en_IR, en_PC, en_R, en_W, inc_PC, not_1_out, or_1_out,
       or_2_out, or_3_out, or_4_out, or_5_out, or_6_out, or_7_out, T0, T2, T3, T4, T5, T6;
  wire [2:0] ALUU, BUS;
  wire [3:0] Sc_q;
  wire [11:0] AR_2_q, bit_extender_3_out, PC_q;
  wire [15:0] AC, alumux_1_out, bit_extender_1_out, bit_extender_2_out, DR_q, IR, ram_1_data, TR_q;

  cu cu_1 (
    .IR(IR), .D0(D0), .D1(D1), .D2(D2), .SC(Sc_q), .D3(D3), .D4(D4), .B11(B11), .D5(D5), .B10(B10), .D6(D6),
    .D7(D7), .B9(B9), .B8(B8), .B7(B7), .B6(B6), .B5(B5), .B4(B4), .B3(B3), .B2(B2), .B1(B1), .B0(B0),
    .T0(T0), .T1(en_IR), .T2(T2), .T3(T3), .T4(T4), .T5(T5), .T6(T6));
  Counter #(.width(4), .max('hf)) Sc (.Q(Sc_q), .clk(CLK), .clr(d_ff_1_q));  // open: load, D, count, carry
  D_Flip_Flop d_ff_1 (.clk(CLK), .D(clr_SC), .Q(d_ff_1_q));  // open: Qn, preset, en, reset
  and and_1 (and_1_out, D5, T5);
  Clock clock_1 (.out(CLK));
  and and_2 (and_2_out, D7, T3, B5);
  and and_3 (and_3_out, D3, T4);
  or or_1 (or_1_out, D5, D2);
  and and_4 (and_4_out, or_1_out, T5);
  or u_AC (AC_out, and_2_out, and_1_out, and_3_out);
  and AR (AR_out, D4, T4);
  and and_5 (and_5_out, D5, T6);
  and and_6 (and_6_out, D1, T5);
  and and_7 (and_7_out, D7, T4, B5);
  and and_8 (and_8_out, D0, T5);
  Register #(.width(12)) AR_2 (.D(bit_extender_3_out), .en(en_AR), .Q(AR_2_q), .clk(CLK), .clr(in_1));
  Register #(.width(16)) TR (.D(out_5), .en(1'b0), .Q(TR_q), .clk(CLK), .clr(Clear));
  Register #(.width(16)) DR (.D(out_5), .en(en_DR), .Q(DR_q), .clk(CLK), .clr(Clear_2));
  Register #(.width(16)) AC_2 (.D(alumux_1_out), .en(en_AC), .Q(AC), .clk(CLK), .clr(Clear_3));
  Priority_Encoder priority_encoder_1 (
    .in0(1'b0), .in1(and_6_out), .in2(and_5_out), .in3(and_4_out), .in4(and_8_out), .in5(1'b0), .in6(1'b0),
    .in7(and_7_out), .out(ALUU));  // open: en_in, gs, en_out
  RAM #(.addrWidth(12), .dataWidth(16), .bus("separate")) ram_1 (
    .addr(AR_2_q), .din(out_5), .data(ram_1_data), .str(en_W), .clk(CLK), .ld(en_R));  // open: sel, clr
  Counter #(.width(12), .max('hfff)) PC (
    .load(en_PC), .D(bit_extender_3_out), .count(inc_PC), .Q(PC_q), .clk(CLK));  // open: carry, clr
  Priority_Encoder priority_encoder_2 (
    .in0(en_R), .in1(AR_out), .in2(1'b0), .in3(1'b0), .in4(AC_out), .in5(T0), .in6(T2), .out(BUS));  // open: in7, en_in, gs, en_out
  assign bit_extender_1_out = {{4{1'b0}}, AR_2_q};  // Bit_Extender bit_extender_1
  assign bit_extender_2_out = {{4{1'b0}}, PC_q};  // Bit_Extender bit_extender_2
  ALUMUX alumux_1 (.A(DR_q), .B(AC), .C2C1C0(ALUU), .OUT(alumux_1_out), .E(E));
  Register #(.width(16)) u_IR (.D(out_5), .en(en_IR), .Q(IR), .clk(CLK));  // open: clr
  Bit_Extender #(.in_width(16), .out_width(12)) bit_extender_3 (.in(out_5), .out(bit_extender_3_out));
  Multiplexer #(.select(3), .width(16), .enable("false")) multiplexer_1 (
    .in0(ram_1_data), .in1(bit_extender_1_out), .in2(TR_q), .in3(DR_q), .in4(AC), .in5(bit_extender_2_out),
    .in6(IR), .out(out_5), .sel(BUS));  // open: in7
  and and_9 (and_9_out, D5, T6);
  or or_2 (or_2_out, T6, T5);
  or or_3 (or_3_out, D4, D3);
  or or_4 (or_4_out, T5, T4);
  or or_5 (or_5_out, AC[15], AC[14], AC[13], AC[12], AC[11], AC[10], AC[9], AC[8], AC[7], AC[6], AC[5], AC[4], AC[3], AC[2], AC[1], AC[0]);
  not not_1 (not_1_out, or_5_out);
  or or_6 (or_6_out, D1, D2, D0);
  and and_10 (and_10_out, or_3_out, T4);
  and and_11 (and_11_out, D7, B2, T3);
  and and_12 (and_12_out, D7, T4, B5);
  or or_7 (or_7_out, D0, D1, D2, D5);
  and and_13 (and_13_out, not_1_out, B2, D7, T3);
  and and_14 (and_14_out, T5, or_6_out);
  and and_15 (en_W, D3, T4);
  and and_16 (and_16_out, or_7_out, T4);
  and and_17 (and_17_out, D2, T5);
  and and_18 (and_18_out, D1, T5);
  and and_19 (and_19_out, D5, or_2_out);
  and and_20 (and_20_out, D7, T4, B5);
  and and_21 (and_21_out, D0, T5);
  and and_22 (en_PC, T4, D4);
  or or_8 (en_R, and_16_out, en_IR);
  and and_23 (and_23_out, D2, T4);
  and and_24 (and_24_out, D1, T4);
  and and_25 (and_25_out, D5, or_4_out);
  and and_26 (and_26_out, D7, T3, B5);
  and and_27 (and_27_out, D0, T4);
  or or_9 (inc_PC, and_13_out, en_IR);
  or or_10 (clr_SC, and_14_out, and_10_out, and_9_out, and_11_out, and_12_out);
  or or_11 (en_AR, T0, T2);
  or or_12 (en_AC, and_17_out, and_18_out, and_19_out, and_20_out, and_21_out);
  or or_13 (en_DR, and_23_out, and_24_out, and_25_out, and_26_out, and_27_out);

  // Other names for the same wires on the sheet: T1 = en_IR

  // Notes on the sheet:
  //   memory 4096 X 16
endmodule

module ALU (
  input  [15:0] A,
  input  [15:0] B,
  input  [2:0] C2C1C0,
  output [15:0] OUT,
  output E
);

  wire adder_1_cout, adder_2_cout, and_2_out, and_3_out, and_4_out, not_1_out, not_2_out, not_3_out,
       not_4_out, subtractor_1_bout;
  wire [15:0] adder_1_out, adder_2_out, and_1_out, or_1_out, subtractor_1_out, xor_1_out;

  Adder #(.width(16)) adder_1 (.a(A), .b(B), .out(adder_1_out), .cin(1'b0), .cout(adder_1_cout));
  Subtractor #(.width(16)) subtractor_1 (.a(A), .b(B), .out(subtractor_1_out), .bin(1'b0), .bout(subtractor_1_bout));
  assign and_1_out = A & B;  // AND_Gate and_1, 16 bits wide
  assign or_1_out = A | B;  // OR_Gate or_1, 16 bits wide
  assign xor_1_out = A ^ B;  // XOR_Gate xor_1, 16 bits wide
  Adder #(.width(16)) adder_2 (.a(A), .b(16'h1), .out(adder_2_out), .cin(1'b0), .cout(adder_2_cout));
  Multiplexer #(.select(3), .width(16), .enable("false")) multiplexer_1 (
    .in1(adder_1_out), .in2(subtractor_1_out), .in3(A), .in4(and_1_out), .in5(or_1_out), .in6(xor_1_out),
    .in7(adder_2_out), .out(OUT), .sel(C2C1C0));  // open: in0
  not not_1 (not_1_out, C2C1C0[1]);
  not not_2 (not_2_out, C2C1C0[2]);
  not not_3 (not_3_out, C2C1C0[0]);
  not not_4 (not_4_out, C2C1C0[2]);
  and and_2 (and_2_out, C2C1C0[0], not_1_out, not_2_out, adder_1_cout);
  and and_3 (and_3_out, not_3_out, C2C1C0[1], not_4_out, subtractor_1_bout);
  and and_4 (and_4_out, C2C1C0[0], C2C1C0[1], C2C1C0[2], adder_2_cout);
  or or_2 (E, and_2_out, and_3_out, and_4_out);
endmodule

module ALUMUX (
  input  [15:0] A,
  input  [15:0] B,
  input  [2:0] C2C1C0,
  output [15:0] OUT,
  output E
);

  wire adder_1_cout, adder_2_cout, subtractor_1_bout;
  wire [15:0] adder_1_out, adder_2_out, and_1_out, or_1_out, subtractor_1_out, xor_1_out;

  Adder #(.width(16)) adder_1 (.a(A), .b(B), .out(adder_1_out), .cin(1'b0), .cout(adder_1_cout));
  Subtractor #(.width(16)) subtractor_1 (.a(A), .b(B), .out(subtractor_1_out), .bin(1'b0), .bout(subtractor_1_bout));
  assign and_1_out = A & B;  // AND_Gate and_1, 16 bits wide
  assign or_1_out = A | B;  // OR_Gate or_1, 16 bits wide
  assign xor_1_out = A ^ B;  // XOR_Gate xor_1, 16 bits wide
  Adder #(.width(16)) adder_2 (.a(A), .b(16'h1), .out(adder_2_out), .cin(1'b0), .cout(adder_2_cout));
  Multiplexer #(.select(3), .width(16), .enable("false")) multiplexer_1 (
    .in0({16{1'b0}}), .in1(adder_1_out), .in2(subtractor_1_out), .in3(A), .in4(and_1_out), .in5(or_1_out),
    .in6(xor_1_out), .in7(adder_2_out), .out(OUT), .sel(C2C1C0));
  Multiplexer #(.select(3), .enable("false")) multiplexer_2 (
    .in0(1'b0), .in1(adder_1_cout), .in2(subtractor_1_bout), .in3(1'b0), .in4(1'b0), .in5(1'b0), .in6(1'b0),
    .in7(adder_2_cout), .out(E), .sel(C2C1C0));
endmodule

// CU
module cu (
  input  [15:0] IR,
  input  [3:0] SC,
  output B11,
  output B0,
  output B10,
  output B2,
  output B1,
  output B3,
  output B4,
  output B5,
  output B6,
  output D1,
  output D3,
  output B7,
  output D2,
  output D0,
  output D4,
  output D5,
  output D6,
  output D7,
  output B8,
  output B9,
  output T0,
  output T1,
  output T2,
  output T3,
  output T4,
  output T5,
  output T6
);

  Decoder #(.select(3), .enable("false")) decoder_1 (
    .out0(D0), .out1(D1), .out2(D2), .out3(D3), .out4(D4), .out5(D5), .out6(D6), .out7(D7), .sel(IR[14:12]));
  Decoder #(.select(4), .enable("false")) decoder_2 (
    .out0(T0), .out1(T1), .out2(T2), .out3(T3), .out4(T4), .out5(T5), .out6(T6), .sel(SC));  // open: out7, out8, out9, out10, out11, out12, out13, out14, out15

  assign B0 = IR[0];
  assign B1 = IR[1];
  assign B2 = IR[2];
  assign B3 = IR[3];
  assign B4 = IR[4];
  assign B5 = IR[5];
  assign B6 = IR[6];
  assign B7 = IR[7];
  assign B8 = IR[8];
  assign B9 = IR[9];
  assign B10 = IR[10];
  assign B11 = IR[11];

  // Other names for the same wires on the sheet: I = IR[15]
endmodule
